# Fritzing sketch ESP8266 Serial Via Arduino (saved by Fritzing 0.9.4)
breadboards: 1

parts:
  YwRobot_Power_Supply1 = YwRobot Breadboard Power Supply [part_number=545043]
  Part1 = Arduino Uno (Rev3)
  U1 = ESP8266 WiFi Module [part_number=ESP8266]
  J5 = 2 row by 3 100mil header to 300mil DIP footprint [package=THT]
  J6 = 2 row by 3 100mil header to 300mil DIP footprint [package=THT]
  R5 = Resistor [tolerance=±5% resistance=1.2k package=THT]
  LED1 = LED - 5mm [color="Green (565nm)" package="5 mm [THT]"]
  R8 = Resistor [tolerance=±5% resistance=560 package=THT]
  SW1 = DIP SWITCH [package=dipswitch-02]
  R2 = Resistor [tolerance=±5% resistance=1.2k package=THT]
  R1 = Resistor [tolerance=±5% resistance=1.2k package=THT]
  SW3 = Momentary Switch [package=ksa_sealed_tac_switch]
  SW2 = DIP SWITCH [package=dipswitch-02]
  R3 = Resistor [tolerance=±5% resistance=1.2k package=THT]
  R4 = Resistor [tolerance=±5% resistance=1.2k package=THT]
  R6 = Resistor [tolerance=±5% resistance=1.2k package=THT]
  R7 = Resistor [tolerance=±5% resistance=1.2k package=THT]

nets:
  3.3V: YwRobot_Power_Supply1.VCC#5, YwRobot_Power_Supply1.VCC#6, U1.VCC, J5.dip_4, J5.soc_4, R1.Pin_0
  N1: YwRobot_Power_Supply1.VCC#9, YwRobot_Power_Supply1.VCC#10
  GND: YwRobot_Power_Supply1.GND, Part1.GND, U1.GND, J6.dip_3, J6.soc_3, SW1.1, SW3.1, SW3.2, SW2.3, R7.Pin_1
  N2: Part1.D0/RX, R5.Pin_0
  N3: Part1.D1/TX, U1.TXD, J6.dip_4, J6.soc_4
  N4: Part1.RESET, LED1.cathode, SW1.4
  5V: Part1.5V, R8.Pin_0
  N5: U1.RXD, J5.dip_3, J5.soc_3, R5.Pin_1, R6.Pin_0
  N6: U1.GPIO_0, J6.dip_1, J6.soc_1, R3.Pin_1
  N7: U1.RST, J6.dip_6, J6.soc_6, SW3.3, SW3.4
  N8: U1.GPIO_2, J6.dip_2, J6.soc_2
  N9: U1.CH_PD, J6.dip_5, J6.soc_5, R2.Pin_1
  N10: J5.dip_6, R2.Pin_0, R1.Pin_1
  N11: LED1.anode, R8.Pin_1
  N12: SW2.2, R4.Pin_0
  N13: R3.Pin_0, R4.Pin_1
  N14: R6.Pin_1, R7.Pin_0

custom parts:
  YwRobot Breadboard Power Supply: The YwRobot Breadboard Power Supply (MB-V2) has two power rails; they can be 5V or 3V3. Power to the module can be provided through the female USB socket or through the A10 (female) 2.1mm power jack.
  ESP8266 WiFi Module: Generic WiFi Module based on the ESP8266 with onboard PCB antenna and UART communications
  2 row by 3 100mil header to 300mil DIP footprint: 0.1 inch 2 row by 3 header to 300mil DIP footprint adapter
