# Fritzing sketch boot_load_tester-2 (saved by Fritzing 0.9.4)
breadboards: 1

parts:
  ESP01 = ESP8266 WiFi Module [part_number=ESP8266]
  R1 = Resistor [tolerance=±5% resistance=560 package=THT]
  R2 = Resistor [tolerance=±5% resistance=560 package=THT]
  R3 = Resistor [tolerance=±5% resistance=560 package=THT]
  R4 = Resistor [tolerance=±5% resistance=560 package=THT]
  LED3 = LED - 5mm [color="Red (633nm)" package="5 mm [THT]"]  # not connected
  LED0 = LED - 5mm [color="Red (633nm)" package="5 mm [THT]"]  # not connected
  LED2 = LED - 5mm [color="Green (555nm)" package="5 mm [THT]"]  # not connected
  J1 = 2 row by 3 100mil header to 300mil DIP footprint adapter
  J2 = 2 row by 3 100mil header to 300mil DIP footprint adapter
  PWR1 = MB102 Breadboard Power Supply
  J3 = blue female 0.1in shorting jumper
  J4 = blue female 0.1in shorting jumper
  LED1 = LED - 5mm [color="Green (560nm)" package="5 mm [THT]"]  # not connected

nets:
  N1: ESP01.RXD, R2.Pin_1, J1.dip_1, J1.soc_1
  3.3V: ESP01.VCC, ESP01.RST, ESP01.CH_PD, J1.dip_4, J1.dip_5, J1.dip_6, J1.soc_4, J1.soc_5, J1.soc_6, PWR1.+1(1), PWR1.+1(2), PWR1.+2(1), PWR1.+2(2), PWR1.+1(3), PWR1.+1(4), PWR1.3V3(1), PWR1.+2(3), PWR1.+2(4), PWR1.3V3(2), PWR1.3V3(3), J3.1, J3.2, J4.1, J4.2
  N2: ESP01.GPIO_0, R3.Pin_0, J1.dip_2, J1.soc_2
  N3: ESP01.GPIO_2, R4.Pin_0, J1.dip_3, J1.soc_3
  GND: ESP01.GND, J2.dip_1, J2.soc_1, PWR1.GND(1), PWR1.GND(2), PWR1.GND(3), PWR1.GND(4)
  N4: ESP01.TXD, R1.Pin_1, J2.dip_6, J2.soc_6

notes:
  GPIO_1
  GPIO_3

custom parts:
  ESP8266 WiFi Module: Generic WiFi Module based on the ESP8266 with onboard PCB antenna and UART communications
  2 row by 3 100mil header to 300mil DIP footprint adapter: 0.1 inch spacing 2 row by 3 female header to 300mil male DIP footprint adapter
  MB102 Breadboard Power Supply: The YwRobot Breadboard Power Supply (MB-V2) has two power rails; they can be 0, 5V or 3V3. Power to the module is provided through the A10 (female) 2.1mm power jack.
  blue female 0.1in shorting jumper: blue 0.1in female header connection jumper

// code stored in the sketch: boot_load_tester.ino
/**
  ESP01 boot testing with pull up, pull down, or no load on combinations of the
  4 available GPIO pins.

  Reference information:
    [ESP Boot Modes](https://github.com/esp8266/esp8266-wiki/wiki/Boot-Process#esp-boot-modes)
    [ESP8266 Boot Mode Selection](https://github.com/espressif/esptool/wiki/ESP8266-Boot-Mode-Selection)

  Pin Test conditions:
    L - pulled to ground through an led and 560 Ohm resistor
    H - pulled to 3.3V through an led and 560 Ohm resistor
    F - floating (no connection)
    S - special; pulled to ground through a 470K Ohm resistor
      - connected to FET gate with source connected to ground
  Test Results:
   * GPIO Pin *  Result
    0  1  2  3
    H  H  H  H  0,1,2 flicker on power up; boots to sketch
    F  H  H  H  1,2 flicker on power up; boots to sketch
    L  H  H  H  
 */
//const int LED_PIN = LED_BUILTIN; // GPIO2
//const int LED_PIN = 0; // GPIO0
//const int LED_PIN = 1; // Blue led on 8266; TX if serial connected to Arduino
//const int LED_PIN = 2; // GPIO2
//const int LED_PIN = 3; // RX but does not feed back to arduino through voltage divider
const unsigned int LED_PINS[] = {0, 1, 2, 3};
const unsigned int PIN_COUNT = sizeof(LED_PINS) / sizeof(LED_PINS[0]);

const unsigned long ON_TIME = 100; // milliseconds
const unsigned long OFF_TIME = 1000; // milliseconds
const int ON_LEVEL = LOW; // Active LOW, on = low voltage level
const int OFF_LEVEL = HIGH; // Active LOW, off = high voltage level

void setup() {
  // initialize the selected pin(s) for output.
  //pinMode(LED_PIN, OUTPUT);
  delay(2000); // Add startup delay, so can 'see' any pulse on power up
  for(unsigned int pin = 0; pin < PIN_COUNT; pin++) {
    pinMode(pin, OUTPUT);
    digitalWrite(pin, OFF_LEVEL); // Set pin to configured OFF level
  }
  flicker_led(3);
  delay(2000); // Add startup delay, so can 'see' any pulse on power up
}


void loop() {
  // Blink each of the configured LEDs in turn
  for(unsigned int pin = 0; pin < PIN_COUNT; pin++) {
//    blink_led(pin);
    flicker_led(pin);
  }
}


void blink_led(const unsigned int pin)
{
  digitalWrite(pin, ON_LEVEL); // Set pin to configured ON level
  delay(ON_TIME);
  digitalWrite(pin, OFF_LEVEL); // Set pin to configured OFF level
  delay(OFF_TIME);
}
void flicker_led(const unsigned int pin)
{
  for(unsigned int i = 0; i <= pin; i++) {
    digitalWrite(pin, ON_LEVEL);
    delay(ON_TIME);
    digitalWrite(pin, OFF_LEVEL);
    delay(ON_TIME);
  }
  delay(OFF_TIME);
}
