# Fritzing sketch boot_load_tester (saved by Fritzing 0.9.4)
breadboards: 1

parts:
  ESP01 = ESP8266 WiFi Module [part_number=ESP8266]
  R1 = Resistor [tolerance=±5% resistance=560 package=THT]
  R2 = Resistor [tolerance=±5% resistance=560 package=THT]
  R3 = Resistor [tolerance=±5% resistance=560 package=THT]
  R4 = Resistor [tolerance=±5% resistance=560 package=THT]
  LED3a = LED - 5mm [color="Red (633nm)" package="5 mm [THT]"]
  LED3b = LED - 5mm [color="Red (633nm)" package="5 mm [THT]"]
  LED0a = LED - 5mm [color="Red (633nm)" part_number=10mm package="5 mm [THT]"]
  LED0b = LED - 5mm [color="Red (633nm)" part_number=10mm package="5 mm [THT]"]
  LED2a = LED - 5mm [color="Green (555nm)" package="5 mm [THT]"]
  LED2a1 = LED - 5mm [color="Green (555nm)" package="5 mm [THT]"]
  J1 = 2 row by 3 100mil header to 300mil DIP footprint adapter
  J2 = 2 row by 3 100mil header to 300mil DIP footprint adapter
  PWR1 = MB102 Breadboard Power Supply
  J3 = blue female 0.1in shorting jumper
  J4 = blue female 0.1in shorting jumper
  LED1a = LED - 5mm [color="Green (560nm)" package="5 mm [THT]"]
  LED1b = LED - 5mm [color="Green (560nm)" package="5 mm [THT]"]

nets:
  N1: ESP01.RXD, R2.Pin_1, J1.dip_1, J1.soc_1
  3.3V: ESP01.VCC, ESP01.RST, ESP01.CH_PD, LED3a.anode, LED0a.anode, LED2a.anode, J1.dip_4, J1.dip_5, J1.dip_6, J1.soc_4, J1.soc_5, J1.soc_6, PWR1.+1(1), PWR1.+1(2), PWR1.+2(1), PWR1.+2(2), PWR1.+1(3), PWR1.+1(4), PWR1.3V3(1), PWR1.+2(3), PWR1.+2(4), PWR1.3V3(2), PWR1.3V3(3), J3.1, J3.2, J4.1, J4.2, LED1a.anode
  N2: ESP01.GPIO_0, R3.Pin_0, J1.dip_2, J1.soc_2
  N3: ESP01.GPIO_2, R4.Pin_0, J1.dip_3, J1.soc_3
  GND: ESP01.GND, LED3b.cathode, LED0b.cathode, LED2a1.cathode, J2.dip_1, J2.soc_1, PWR1.GND(1), PWR1.GND(2), PWR1.GND(3), PWR1.GND(4), LED1b.cathode
  N4: ESP01.TXD, R1.Pin_1, J2.dip_6, J2.soc_6

notes:
  GPIO_1
  GPIO_3

custom parts:
  ESP8266 WiFi Module: Generic WiFi Module based on the ESP8266 with onboard PCB antenna and UART communications
  2 row by 3 100mil header to 300mil DIP footprint adapter: 0.1 inch spacing 2 row by 3 female header to 300mil male DIP footprint adapter
  MB102 Breadboard Power Supply: The YwRobot Breadboard Power Supply (MB-V2) has two power rails; they can be 0, 5V or 3V3. Power to the module is provided through the A10 (female) 2.1mm power jack.
  blue female 0.1in shorting jumper: blue 0.1in female header connection jumper
